# Fritzing sketch Circuit (saved by Fritzing 0.9.4)
breadboards: 1

parts:
  Raspberry_Pi_1 = Raspberry Pi 3 [part_number=RPI-3-V1.2]
  J1 = Basic Servo
  VCC1 = 4 x AAA Battery Mount

nets:
  N1: Raspberry_Pi_1.GPIO3, J1.pulse
  GND: Raspberry_Pi_1.GND, J1.gnd, VCC1.-
  N2: J1.vcc, VCC1.+
